// Logisim project student_solution.circ as structural Verilog: 1 circuit, main circuit solution
module solution (
  input  a,
  input  b,
  input  c,
  output d
);

  wire and_1_out, and_2_out, not_1_out;

  not not_1 (not_1_out, a);
  and and_1 (and_1_out, a, c);
  and and_2 (and_2_out, not_1_out, b);
  or or_1 (d, and_1_out, and_2_out);
endmodule
