// Logisim project teacher_solution.circ as structural Verilog: 1 circuit, main circuit solution
module solution (
  input  a,
  input  b,
  input  c,
  output d
);

  wire and_1_out, and_2_out, not_1_out, not_2_out;

  not not_1 (not_1_out, a);
  not not_2 (not_2_out, a);
  and and_1 (and_1_out, not_1_out, c);
  and and_2 (and_2_out, not_2_out, b);
  or or_1 (d, and_1_out, and_2_out);
endmodule
