// Logisim project test_generator.circ as structural Verilog: 1 circuit, main circuit main
module main (
  output a,
  output b,
  output c,
  output d,
  output halt
);

  wire clock_1_out;

  Clock clock_1 (.out(clock_1_out));
  Counter #(.width(3), .max('h7)) counter_1 (
    .Q({c, b, a}), .carry(halt), .clk(clock_1_out));  // open: load, D, count, clr
  solution solution_1 (.a(c), .b(b), .c(a), .d(d));

  // Notes on the sheet:
  //   Implemented by Teacher
endmodule
